// Logisim project 3bit.circ as structural Verilog: 1 circuit, main circuit main
module main (
  input  _3_Bit_B,
  input  in_2,
  input  in_3,
  input  _3_Bit_A,
  input  in_5,
  input  in_6,
  input  Carry_In,
  output Carry_out,
  output Sum_2,
  output Sum_1,
  output Sum_0
);

  wire and_1_out, and_2_out, and_3_out, and_4_out, and_5_out, and_6_out, or_2_out, or_3_out, xor_1_out,
       xor_3_out, xor_5_out;

  and and_1 (and_1_out, _3_Bit_A, _3_Bit_B);
  and and_2 (and_2_out, xor_1_out, or_2_out);
  or or_1 (Carry_out, and_1_out, and_2_out);
  xor xor_1 (xor_1_out, _3_Bit_B, _3_Bit_A);
  xor xor_2 (Sum_2, or_2_out, xor_1_out);
  and and_3 (and_3_out, in_5, in_2);
  and and_4 (and_4_out, xor_3_out, or_3_out);
  or or_2 (or_2_out, and_3_out, and_4_out);
  xor xor_3 (xor_3_out, in_2, in_5);
  xor xor_4 (Sum_1, or_3_out, xor_3_out);
  and and_5 (and_5_out, in_6, in_3);
  and and_6 (and_6_out, xor_5_out, Carry_In);
  or or_3 (or_3_out, and_5_out, and_6_out);
  xor xor_5 (xor_5_out, in_3, in_6);
  xor xor_6 (Sum_0, Carry_In, xor_5_out);
endmodule
