// Logisim project 4bit.circ as structural Verilog: 1 circuit, main circuit main
module main (
  input  in_1,
  input  _3_Bit_B,
  input  in_3,
  input  in_4,
  input  in_5,
  input  _3_Bit_A,
  input  in_7,
  input  in_8,
  input  Carry_In,
  output out_10,
  output Sum_1,
  output Sum_1_2,
  output Sum_0,
  output Sum_2
);

  wire and_1_out, and_2_out, and_3_out, and_4_out, and_5_out, and_6_out, and_7_out, and_8_out, or_2_out,
       or_3_out, or_4_out, xor_1_out, xor_3_out, xor_5_out, xor_7_out;

  and and_1 (and_1_out, in_5, in_1);
  and and_2 (and_2_out, xor_1_out, or_2_out);
  or or_1 (out_10, and_1_out, and_2_out);
  xor xor_1 (xor_1_out, in_1, in_5);
  xor xor_2 (Sum_2, or_2_out, xor_1_out);
  and and_3 (and_3_out, _3_Bit_A, _3_Bit_B);
  and and_4 (and_4_out, xor_3_out, or_3_out);
  or or_2 (or_2_out, and_3_out, and_4_out);
  xor xor_3 (xor_3_out, _3_Bit_B, _3_Bit_A);
  xor xor_4 (Sum_1, or_3_out, xor_3_out);
  and and_5 (and_5_out, in_7, in_3);
  and and_6 (and_6_out, xor_5_out, or_4_out);
  or or_3 (or_3_out, and_5_out, and_6_out);
  xor xor_5 (xor_5_out, in_3, in_7);
  xor xor_6 (Sum_1_2, or_4_out, xor_5_out);
  and and_7 (and_7_out, in_8, in_4);
  and and_8 (and_8_out, xor_7_out, Carry_In);
  or or_4 (or_4_out, and_7_out, and_8_out);
  xor xor_7 (xor_7_out, in_4, in_8);
  xor xor_8 (Sum_0, Carry_In, xor_7_out);

  // Notes on the sheet:
  //   Carry out
endmodule
