// Logisim project circuit 1.circ as structural Verilog: 1 circuit, main circuit main
module main (
  input  in_1,
  input  A,
  input  in_3,
  input  in_4,
  input  B,
  input  C,
  input  A_2,
  input  B_2,
  input  C_2,
  output out_10,
  output out_11,
  output out_12
);

  wire and_1_out, and_2_out, and_3_out, and_4_out, and_5_out, and_7_out, and_8_out, and_9_out, or_1_out,
       or_2_out, or_3_out;

  or or_1 (or_1_out, A_2, B_2, C_2);
  or or_2 (or_2_out, A_2, ~B_2, C_2);  // OR_Gate
  or or_3 (or_3_out, ~A_2, ~B_2, ~C_2);  // OR_Gate
  and and_1 (and_1_out, ~A, ~B, C);  // AND_Gate
  and and_2 (and_2_out, ~A, B, C);  // AND_Gate
  and and_3 (and_3_out, A, ~B, ~C);  // AND_Gate
  and and_4 (and_4_out, A, ~B, C);  // AND_Gate
  and and_5 (and_5_out, A, B, ~C);  // AND_Gate
  and and_6 (out_12, or_1_out, or_2_out, or_3_out);
  or or_4 (out_11, and_1_out, and_2_out, and_3_out, and_4_out, and_5_out);
  and and_7 (and_7_out, in_1, ~in_3);  // AND_Gate
  and and_8 (and_8_out, in_1, ~in_4);  // AND_Gate
  and and_9 (and_9_out, ~in_1, in_4);  // AND_Gate
  or or_5 (out_10, and_7_out, and_8_out, and_9_out);

  // Notes on the sheet:
  //   SOP
  //   POS
  //   SOP
endmodule
