// Logisim project circuit 2.circ as structural Verilog: 1 circuit, main circuit main
module main (
  input  A,
  input  B,
  input  C,
  input  A_2,
  input  B_2,
  input  C_2,
  output out_7,
  output out_8
);

  wire and_1_out, and_2_out, or_2_out, or_3_out, or_4_out, or_5_out, or_6_out;

  and and_1 (and_1_out, ~A, ~B, ~C);  // AND_Gate
  and and_2 (and_2_out, A, C);
  or or_1 (out_7, and_1_out, and_2_out);
  or or_2 (or_2_out, A_2, B_2, ~C_2);  // OR_Gate
  or or_3 (or_3_out, A_2, ~B_2, C_2);  // OR_Gate
  or or_4 (or_4_out, A_2, ~B_2, ~C_2);  // OR_Gate
  or or_5 (or_5_out, ~A_2, B_2, C_2);  // OR_Gate
  or or_6 (or_6_out, ~A_2, ~B_2, C_2);  // OR_Gate
  and and_3 (out_8, or_2_out, or_3_out, or_4_out, or_5_out, or_6_out);

  // Notes on the sheet:
  //   SOP
  //   POS
endmodule
