// Logisim project part1.circ as structural Verilog: 1 circuit, main circuit main
module main (
  input  in_1,
  input  in_2,
  input  in_3,
  input  in_4,
  input  in_5,
  input  in_6,
  input  in_7,
  output out_8,
  output out_9,
  output out_10,
  output out_11,
  output out_12,
  output out_13,
  output out_14
);

  wire and_1_out, and_2_out, and_3_out, and_4_out;

  and and_1 (and_1_out, ~in_1, in_4);  // AND_Gate
  and and_2 (and_2_out, in_1, in_5);
  and and_3 (and_3_out, in_6, ~in_7);  // AND_Gate
  and and_4 (and_4_out, in_6, in_7);
  or or_1 (out_9, and_1_out, and_2_out);
  nor nor_1 (out_13, and_3_out, out_14);
  nor nor_2 (out_14, out_13, and_4_out);
  and and_5 (out_8, ~in_2, ~in_3);  // AND_Gate
  and and_6 (out_10, ~in_2, in_3, in_3);  // AND_Gate
  and and_7 (out_11, in_2, ~in_3);  // AND_Gate
  and and_8 (out_12, in_2, in_3);
endmodule
