// Logisim project part2.circ as structural Verilog: 2 circuits, main circuit main
module main (
  input  in_1,
  output out_2,
  output out_3,
  output out_4,
  output out_5,
  output out_6,
  output out_7,
  output out_8,
  output out_9,
  output out_10
);

  wire adder_2_out_4, adder_3_out_4, adder_4_out_4, adder_5_out_4, adder_6_out_4, adder_7_out_4,
       adder_8_out_4;
  wire [7:0] register_1_q, register_2_q;

  Register register_1 (.Q(register_1_q));  // open: D, en, clk, clr
  adder adder_1 (.in_3(adder_3_out_4), .in_1(register_1_q[7]), .in_2(register_2_q[7]), .out_4(out_2), .out_5(out_3));
  adder adder_2 (
    .in_3(adder_4_out_4), .in_1(register_1_q[5]), .in_2(register_2_q[5]), .out_4(adder_2_out_4), .out_5(out_5));
  adder adder_3 (
    .in_3(adder_2_out_4), .in_1(register_1_q[6]), .in_2(register_2_q[6]), .out_4(adder_3_out_4), .out_5(out_4));
  adder adder_4 (
    .in_3(adder_6_out_4), .in_1(register_1_q[4]), .in_2(register_2_q[4]), .out_4(adder_4_out_4), .out_5(out_6));
  Register register_2 (.Q(register_2_q));  // open: D, en, clk, clr
  adder adder_5 (
    .in_3(adder_7_out_4), .in_1(register_1_q[2]), .in_2(register_2_q[2]), .out_4(adder_5_out_4), .out_5(out_8));
  adder adder_6 (
    .in_3(adder_5_out_4), .in_1(register_1_q[3]), .in_2(register_2_q[3]), .out_4(adder_6_out_4), .out_5(out_7));
  adder adder_7 (
    .in_3(adder_8_out_4), .in_1(register_1_q[1]), .in_2(register_2_q[1]), .out_4(adder_7_out_4), .out_5(out_9));
  adder adder_8 (.in_3(in_1), .in_1(register_1_q[0]), .in_2(register_2_q[0]), .out_4(adder_8_out_4), .out_5(out_10));
endmodule

module adder (
  input  in_1,
  input  in_2,
  input  in_3,
  output out_4,
  output out_5
);

  wire and_1_out, and_2_out, xor_1_out;

  and and_1 (and_1_out, in_2, in_1);
  and and_2 (and_2_out, xor_1_out, in_3);
  or or_1 (out_4, and_1_out, and_2_out);
  xor xor_1 (xor_1_out, in_1, in_2);
  xor xor_2 (out_5, in_3, xor_1_out);
endmodule
