// Logisim project AND.circ as structural Verilog: 1 circuit, main circuit main
module main (
  input  in_1,
  input  in_2,
  output out_3
);

  wire transistor_1_out, transistor_4_out;

  Transistor transistor_1 (.in(1'b1), .out(transistor_1_out), .gate(in_1));
  Transistor transistor_2 (.in(1'b1), .out(transistor_1_out), .gate(in_2));
  Transistor #(.\type ("n")) transistor_3 (.in(transistor_4_out), .out(transistor_1_out), .gate(in_1));
  Transistor #(.\type ("n")) transistor_4 (.in(1'b0), .out(transistor_4_out), .gate(in_2));
  Transistor transistor_5 (.in(1'b1), .out(out_3), .gate(transistor_1_out));
  Transistor #(.\type ("n")) transistor_6 (.in(1'b0), .out(out_3), .gate(transistor_1_out));
endmodule
