// Logisim project rs0a.circ as structural Verilog: 13 circuits, main circuit main
module main (
  output [7:0] out_1,
  output [7:0] Register_File,
  output [7:0] out_3,
  output [7:0] out_4,
  output [7:0] out_5,
  output [7:0] ALU_Output
);

  wire clock_1_out, controlunit_1_fetch, controlunit_1_write_reg, decoder_1_alu_sub,
       decoder_1_load_immediate, decoder_1_out_4;
  wire [1:0] decoder_1_alu_sub_2, decoder_1_out_7, decoder_1_out_8, decoder_1_out_9;
  wire [7:0] increment_1_out_2, regfile_1_out_11, regfile_1_out_12, register_1_q;
  wire [15:0] ram_1_data, register_2_q;

  Increment increment_1 (.in_1(register_1_q), .out_2(increment_1_out_2));
  Register register_1 (.D(increment_1_out_2), .Q(register_1_q), .clk(controlunit_1_fetch));  // open: en, clr
  RAM #(.dataWidth(16)) ram_1 (.addr(register_1_q), .data(ram_1_data));  // open: sel, clk, ld, clr
  controlUnit controlunit_1 (.Fetch(controlunit_1_fetch), .Write_Reg(controlunit_1_write_reg), .in_1(clock_1_out));
  Register #(.width(16)) register_2 (.D(ram_1_data), .Q(register_2_q), .clk(controlunit_1_fetch));  // open: en, clr
  Clock clock_1 (.out(clock_1_out));
  decoder decoder_1 (
    .out_4(decoder_1_out_4), .ALU_Sub(decoder_1_alu_sub), .out_7(decoder_1_out_7), .out_8(decoder_1_out_8),
    .out_9(decoder_1_out_9), .Write(controlunit_1_write_reg), .Load_Immediate(decoder_1_load_immediate),
    .in_2(register_2_q), .ALU_Sub_2(decoder_1_alu_sub_2));
  Multiplexer #(.width(8)) multiplexer_1 (
    .in0(register_2_q[7:0]), .in1(ALU_Output), .out(out_1), .sel(decoder_1_out_4));
  regfile regfile_1 (
    .Write_Enable(decoder_1_load_immediate), .Data_In(out_1), .out_7(Register_File), .out_8(out_3),
    .out_9(out_4), .out_10(out_5), .in_5(decoder_1_out_8), .out_11(regfile_1_out_11), .in_4(decoder_1_out_9),
    .out_12(regfile_1_out_12), .in_3(decoder_1_out_7));  // open: out_6
  alu2 alu2_1 (
    .in_3(decoder_1_alu_sub), .in_4(decoder_1_alu_sub_2), .out_5(ALU_Output), .in_1(regfile_1_out_11),
    .in_2(regfile_1_out_12));

  // Notes on the sheet:
  //   Main Memory
  //   Program Counter
  //   Control Unit
  //   Instruction Register
endmodule

module controlUnit (
  input  in_1,
  output Fetch,
  output Write_Reg
);

  wire and_1_out, and_2_out, d_ff_1_q, d_ff_2_q;

  and and_1 (and_1_out, ~d_ff_1_q, d_ff_2_q);  // AND_Gate
  and and_2 (and_2_out, ~d_ff_1_q, ~d_ff_2_q);  // AND_Gate
  D_Flip_Flop d_ff_1 (.clk(in_1), .D(and_1_out), .Q(d_ff_1_q));  // open: Qn, preset, en, reset
  D_Flip_Flop d_ff_2 (.clk(in_1), .D(and_2_out), .Q(d_ff_2_q));  // open: Qn, preset, en, reset
  and and_3 (Fetch, ~d_ff_1_q, ~d_ff_2_q);  // AND_Gate
  and and_4 (Write_Reg, d_ff_1_q, ~d_ff_2_q);  // AND_Gate

  // Notes on the sheet:
  //   S1
  //   S0
endmodule

module regfile (
  input  [7:0] Data_In,
  input  Write_Enable,
  input  [1:0] in_3,
  input  [1:0] in_4,
  input  [1:0] in_5,
  output [2:0] out_6,
  output [7:0] out_7,
  output [7:0] out_8,
  output [7:0] out_9,
  output [7:0] out_10,
  output [7:0] out_11,
  output [7:0] out_12
);

  wire and_1_out, and_2_out, and_4_out, and_5_out, decoder_1_out0, decoder_1_out1, decoder_1_out2,
       decoder_1_out3;
  wire [2:0] zero_1_out_2;

  Decoder #(.select(2)) decoder_1 (
    .out0(decoder_1_out0), .out1(decoder_1_out1), .out2(decoder_1_out2), .out3(decoder_1_out3), .sel(in_3));
  Register register_1 (.D(Data_In), .Q(out_7), .clk(and_1_out));  // open: en, clr
  and and_1 (and_1_out, Write_Enable, decoder_1_out0);
  Multiplexer #(.select(2), .width(8)) multiplexer_1 (
    .in0(out_7), .in1(out_8), .in2(out_9), .in3(out_10), .out(out_11), .sel(in_5));
  zero zero_1 (.in_1(Data_In), .out_2(zero_1_out_2[0]));
  negative negative_1 (.in_1(Data_In), .out_2(zero_1_out_2[1]));
  and and_2 (and_2_out, Write_Enable, decoder_1_out1);
  Register register_2 (.D(Data_In), .Q(out_8), .clk(and_2_out));  // open: en, clr
  and and_3 (zero_1_out_2[2], ~zero_1_out_2[0], ~zero_1_out_2[1]);  // AND_Gate
  and and_4 (and_4_out, Write_Enable, decoder_1_out2);
  Register register_3 (.D(Data_In), .Q(out_9), .clk(and_4_out));  // open: en, clr
  Multiplexer #(.select(2), .width(8)) multiplexer_2 (
    .in0(out_7), .in1(out_8), .in2(out_9), .in3(out_10), .out(out_12), .sel(in_4));
  Register #(.width(3)) register_4 (.D(zero_1_out_2), .Q(out_6), .clk(Write_Enable));  // open: en, clr
  and and_5 (and_5_out, Write_Enable, decoder_1_out3);
  Register register_5 (.D(Data_In), .Q(out_10), .clk(and_5_out));  // open: en, clr

  // Notes on the sheet:
  //   Register Select
  //   Out 1
endmodule

module decoder (
  input  Write,
  input  [15:0] in_2,
  output Load_Immediate,
  output out_4,
  output ALU_Sub,
  output [1:0] ALU_Sub_2,
  output [1:0] out_7,
  output [1:0] out_8,
  output [1:0] out_9
);


  assign ALU_Sub = in_2[14];
  assign ALU_Sub_2 = in_2[1:0];
  assign Load_Immediate = Write;
  assign out_4 = in_2[15];
  assign out_7 = in_2[13:12];
  assign out_8 = in_2[11:10];
  assign out_9 = in_2[9:8];

  // Notes on the sheet:
  //   Opcode
  //   DR
  //   SR0
  //   SR1
endmodule

module alu (
  input  [7:0] in_1,
  input  [7:0] in_2,
  input  in_3,
  output [7:0] out_4
);

  wire [7:0] invert_1_out_2, multiplexer_1_out;

  invert invert_1 (.in_1(in_2), .out_2(invert_1_out_2));
  Multiplexer #(.width(8)) multiplexer_1 (.in0(in_2), .in1(invert_1_out_2), .out(multiplexer_1_out), .sel(in_3));
  Adder adder_1 (.a(multiplexer_1_out), .b(in_1), .out(out_4), .cin(in_3));  // open: cout
endmodule

module Increment (
  input  [7:0] in_1,
  output [7:0] out_2
);

  wire d_ff_1_q, not_1_out;
  wire [7:0] register_1_q;

  Register register_1 (.Q(register_1_q));  // open: D, en, clk, clr
  D_Flip_Flop d_ff_1 (.Q(d_ff_1_q));  // open: clk, D, Qn, preset, en, reset
  not not_1 (not_1_out, d_ff_1_q);
  Adder adder_1 (.a(in_1), .b(register_1_q), .out(out_2), .cin(not_1_out));  // open: cout
endmodule

module simplememory (
  input  [7:0] Data_In,
  input  Write_Enable,
  input  [1:0] in_3,
  output [7:0] out_4,
  output [7:0] out_5,
  output [7:0] out_6,
  output [7:0] out_7,
  output [7:0] out_8
);

  wire and_1_out, and_2_out, and_3_out, and_4_out, decoder_1_out0, decoder_1_out1, decoder_1_out2,
       decoder_1_out3;

  Decoder #(.select(2)) decoder_1 (
    .out0(decoder_1_out0), .out1(decoder_1_out1), .out2(decoder_1_out2), .out3(decoder_1_out3), .sel(in_3));
  and and_1 (and_1_out, Write_Enable, decoder_1_out0);
  Register register_1 (.D(Data_In), .Q(out_4), .clk(and_1_out));  // open: en, clr
  Multiplexer #(.select(2), .width(8)) multiplexer_1 (
    .in0(out_4), .in1(out_5), .in2(out_6), .in3(out_7), .out(out_8), .sel(in_3));
  and and_2 (and_2_out, Write_Enable, decoder_1_out1);
  Register register_2 (.D(Data_In), .Q(out_5), .clk(and_2_out));  // open: en, clr
  Register register_3 (.D(Data_In), .Q(out_6), .clk(and_3_out));  // open: en, clr
  and and_3 (and_3_out, Write_Enable, decoder_1_out2);
  Register register_4 (.D(Data_In), .Q(out_7), .clk(and_4_out));  // open: en, clr
  and and_4 (and_4_out, Write_Enable, decoder_1_out3);

  // Notes on the sheet:
  //   Register Select
  //   Out 1
endmodule

module invert (
  input  [7:0] in_1,
  output [7:0] out_2
);

  not not_1 (out_2[7], in_1[7]);
  not not_2 (out_2[5], in_1[5]);
  not not_3 (out_2[3], in_1[3]);
  not not_4 (out_2[1], in_1[1]);
  not not_5 (out_2[0], in_1[0]);
  not not_6 (out_2[4], in_1[4]);
  not not_7 (out_2[6], in_1[6]);
  not not_8 (out_2[2], in_1[2]);
endmodule

module alu2 (
  input  [7:0] in_1,
  input  [7:0] in_2,
  input  in_3,
  input  [1:0] in_4,
  output [7:0] out_5
);

  wire [7:0] adder_1_out, and8_1_out_3, invert_1_out_2, multiplexer_1_out, multiplier_1_out, or8_1_out_3;

  Multiplexer #(.width(8)) multiplexer_1 (.in0(in_2), .in1(invert_1_out_2), .out(multiplexer_1_out), .sel(in_3));
  Adder adder_1 (.a(multiplexer_1_out), .b(in_1), .out(adder_1_out), .cin(in_3));  // open: cout
  invert invert_1 (.in_1(in_2), .out_2(invert_1_out_2));
  and8 and8_1 (.out_3(and8_1_out_3), .in_1(in_1), .in_2(multiplexer_1_out));
  Multiplier multiplier_1 (.a(multiplexer_1_out), .b(in_1), .out(multiplier_1_out));  // open: cin, cout
  Multiplexer #(.select(2), .width(8)) multiplexer_2 (
    .in0(adder_1_out), .in1(multiplier_1_out), .in2(and8_1_out_3), .in3(or8_1_out_3), .out(out_5), .sel(in_4));
  or8 or8_1 (.out_3(or8_1_out_3), .in_1(in_1), .in_2(multiplexer_1_out));
endmodule

module and8 (
  input  [7:0] in_1,
  input  [7:0] in_2,
  output [7:0] out_3
);

  and and_1 (out_3[7], in_1[7], in_2[7]);
  and and_2 (out_3[6], in_1[6], in_2[6]);
  and and_3 (out_3[5], in_1[5], in_2[5]);
  and and_4 (out_3[4], in_1[4], in_2[4]);
  and and_5 (out_3[3], in_1[3], in_2[3]);
  and and_6 (out_3[2], in_1[2], in_2[2]);
  and and_7 (out_3[1], in_1[1], in_2[1]);
  and and_8 (out_3[0], in_1[0], in_2[0]);
endmodule

module or8 (
  input  [7:0] in_1,
  input  [7:0] in_2,
  output [7:0] out_3
);

  or or_1 (out_3[7], in_1[7], in_2[7]);
  or or_2 (out_3[6], in_1[6], in_2[6]);
  or or_3 (out_3[5], in_1[5], in_2[5]);
  or or_4 (out_3[4], in_1[4], in_2[4]);
  or or_5 (out_3[3], in_1[3], in_2[3]);
  or or_6 (out_3[2], in_1[2], in_2[2]);
  or or_7 (out_3[1], in_1[1], in_2[1]);
  or or_8 (out_3[0], in_1[0], in_2[0]);
endmodule

module zero (
  input  [7:0] in_1,
  output out_2
);

  nor nor_1 (out_2, in_1[0], in_1[1], in_1[2], in_1[3], in_1[4], in_1[5], in_1[6], in_1[7]);
endmodule

module negative (
  input  [7:0] in_1,
  output out_2
);


  assign out_2 = in_1[7];
endmodule
