// Logisim project D flip-flop.circ as structural Verilog: 1 circuit, main circuit main
module main (
  input  in_1,
  input  in_2,
  output out_3,
  output out_4
);

  wire and_1_out, and_2_out, and_3_out, and_4_out, nor_1_out, nor_2_out;

  and and_1 (and_1_out, ~in_1, ~in_2);  // AND_Gate
  and and_2 (and_2_out, in_1, in_2);
  nor nor_1 (nor_1_out, and_1_out, nor_2_out);
  nor nor_2 (nor_2_out, nor_1_out, and_2_out);
  and and_3 (and_3_out, in_1, ~nor_2_out);  // AND_Gate
  and and_4 (and_4_out, in_1, nor_2_out);
  nor nor_3 (out_3, and_3_out, out_4);
  nor nor_4 (out_4, out_3, and_4_out);
endmodule
