// Logisim project D latch.circ as structural Verilog: 1 circuit, main circuit main
module main (
  input  E,
  input  D,
  output Q,
  output out_4
);

  wire and_1_out, and_2_out;

  and and_1 (and_1_out, E, ~D);  // AND_Gate
  and and_2 (and_2_out, E, D);
  nor nor_1 (Q, and_1_out, out_4);
  nor nor_2 (out_4, Q, and_2_out);
endmodule
