// Logisim project bistable circuit.circ as structural Verilog: 1 circuit, main circuit main
module main (
  output out_1,
  output out_2,
  output out_3,
  output out_4
);

  not not_1 (out_2, out_1);
  not not_2 (out_1, out_2);
  not not_3 (out_3, out_4);
  not not_4 (out_4, out_3);
endmodule
